// Logisim project AES.circ as structural Verilog
module s_box (
  input  [7:0] in,
  output [7:0] out
);

  ROM rom_1 (.addr(in), .data(out));  // open: sel

  // Notes on the sheet:
  //   contents of rom_1 (hex, n*v repeats v):
  //   63 7c 77 7b f2 6b 6f c5 30 1 67 2b fe d7 ab 76 ca 82 c9 7d fa 59 47 f0 ad d4 a2 af 9c a4 72 c0 b7 fd
  //   93 26 36 3f f7 cc 34 a5 e5 f1 71 d8 31 15 4 c7 23 c3 18 96 5 9a 7 12 80 e2 eb 27 b2 75 9 83 2c 1a 1b
  //   6e 5a a0 52 3b d6 b3 29 e3 2f 84 53 d1 0 ed 20 fc b1 5b 6a cb be 39 4a 4c 58 cf d0 ef aa fb 43 4d 33
  //   85 45 f9 2 7f 50 3c 9f a8 51 a3 40 8f 92 9d 38 f5 bc b6 da 21 10 ff f3 d2 cd c 13 ec 5f 97 44 17 c4
  //   a7 7e 3d 64 5d 19 73 60 81 4f dc 22 2a 90 88 46 ee b8 14 de 5e b db e0 32 3a a 49 6 24 5c c2 d3 ac
  //   62 91 95 e4 79 e7 c8 37 6d 8d d5 4e a9 6c 56 f4 ea 65 7a ae 8 ba 78 25 2e 1c a6 b4 c6 e8 dd 74 1f 4b
  //   bd 8b 8a 70 3e b5 66 48 3 f6 e 61 35 57 b9 86 c1 1d 9e e1 f8 98 11 69 d9 8e 94 9b 1e 87 e9 ce 55 28
  //   df 8c a1 89 d bf e6 42 68 41 99 2d f b0 54 bb 16
endmodule

module key_gen_turn (
  input  [7:0] kin0,
  input  [7:0] kin1,
  input  [7:0] kin2,
  input  [7:0] kin3,
  input  [7:0] kin4,
  input  [7:0] kin4_2,
  input  [7:0] kin6,
  input  [7:0] kin7,
  input  [7:0] kin8,
  input  [7:0] kin9,
  input  [7:0] kin10,
  input  [7:0] kin11,
  input  [7:0] kin12,
  input  [7:0] kin13,
  input  [7:0] kin14,
  input  [7:0] kin15,
  input  [3:0] turn_number,
  output [7:0] kout0,
  output [7:0] kout1,
  output [7:0] kout2,
  output [7:0] kout3,
  output [7:0] kout4,
  output [7:0] kout4_2,
  output [7:0] kout6,
  output [7:0] kout7,
  output [7:0] kout8,
  output [7:0] kout9,
  output [7:0] kout10,
  output [7:0] kout11,
  output [7:0] kout12,
  output [7:0] kout13,
  output [7:0] kout14,
  output [7:0] kout15
);

  wire [31:0] key_gen_g_1_out;

  key_gen_g key_gen_g_1 (.in({kin12, kin13, kin14, kin15}), .turn_number(turn_number), .out(key_gen_g_1_out));
  assign {kout0, kout1, kout2, kout3} = key_gen_g_1_out ^ {kin0, kin1, kin2, kin3};  // XOR_Gate xor_1, 32 bits wide
  assign {kout4, kout4_2, kout6, kout7} = {kout0, kout1, kout2, kout3} ^ {kin4, kin4_2, kin6, kin7};  // XOR_Gate xor_2, 32 bits wide
  assign {kout8, kout9, kout10, kout11} = {kout4, kout4_2, kout6, kout7} ^ {kin8, kin9, kin10, kin11};  // XOR_Gate xor_3, 32 bits wide
  assign {kout12, kout13, kout14, kout15} = {kout8, kout9, kout10, kout11} ^ {kin12, kin13, kin14, kin15};  // XOR_Gate xor_4, 32 bits wide
endmodule

// g
module key_gen_g (
  input  [31:0] in,
  input  [3:0] turn_number,
  output [31:0] out
);

  wire [7:0] rom_1_data, s_box_1_out;

  s_box s_box_1 (.in(in[23:16]), .out(s_box_1_out));
  s_box s_box_2 (.in(in[15:8]), .out(out[23:16]));
  s_box s_box_3 (.in(in[7:0]), .out(out[15:8]));
  s_box s_box_4 (.in(in[31:24]), .out(out[7:0]));
  ROM #(.addrWidth(4)) rom_1 (.addr(turn_number), .data(rom_1_data));  // open: sel
  assign out[31:24] = rom_1_data ^ s_box_1_out;  // XOR_Gate xor_1, 8 bits wide

  // Notes on the sheet:
  //   contents of rom_1 (hex, n*v repeats v):
  //   1 2 4 8 10 20 40 80 1b 36
endmodule

module test_key_gen (
  input  [7:0] kin0,
  input  [7:0] kin1,
  input  [7:0] kin2,
  input  [7:0] kin3,
  input  [7:0] kin4,
  input  [7:0] kin4_2,
  input  [7:0] kin6,
  input  [7:0] kin7,
  input  [7:0] kin8,
  input  [7:0] kin9,
  input  [7:0] kin10,
  input  [7:0] kin11,
  input  [7:0] kin12,
  input  [7:0] kin13,
  input  [7:0] kin14,
  input  [7:0] kin15,
  input  [3:0] turn_number
);

  wire [7:0] key_gen_turn_1_kout0, key_gen_turn_1_kout1, key_gen_turn_1_kout2, key_gen_turn_1_kout3,
       key_gen_turn_1_kout4, key_gen_turn_1_kout4_2, key_gen_turn_1_kout6, key_gen_turn_1_kout7,
       key_gen_turn_1_kout8, key_gen_turn_1_kout9, key_gen_turn_1_kout10, key_gen_turn_1_kout11,
       key_gen_turn_1_kout12, key_gen_turn_1_kout13, key_gen_turn_1_kout14, key_gen_turn_1_kout15;

  key_gen_turn key_gen_turn_1 (
    .kin0(kin0), .kin1(kin1), .kin2(kin2), .kin3(kin3), .kin4(kin4), .kin4_2(kin4_2), .kin6(kin6),
    .kin7(kin7), .kin8(kin8), .kin9(kin9), .kin10(kin10), .kin11(kin11), .kin12(kin12), .kin13(kin13),
    .kin14(kin14), .kin15(kin15), .turn_number(turn_number), .kout0(key_gen_turn_1_kout0),
    .kout1(key_gen_turn_1_kout1), .kout2(key_gen_turn_1_kout2), .kout3(key_gen_turn_1_kout3),
    .kout4(key_gen_turn_1_kout4), .kout4_2(key_gen_turn_1_kout4_2), .kout6(key_gen_turn_1_kout6),
    .kout7(key_gen_turn_1_kout7), .kout8(key_gen_turn_1_kout8), .kout9(key_gen_turn_1_kout9),
    .kout10(key_gen_turn_1_kout10), .kout11(key_gen_turn_1_kout11), .kout12(key_gen_turn_1_kout12),
    .kout13(key_gen_turn_1_kout13), .kout14(key_gen_turn_1_kout14), .kout15(key_gen_turn_1_kout15));
  // Probe on key_gen_turn_1_kout0
  // Probe on key_gen_turn_1_kout1
  // Probe on key_gen_turn_1_kout2
  // Probe on key_gen_turn_1_kout3
  // Probe on key_gen_turn_1_kout4
  // Probe on key_gen_turn_1_kout4_2
  // Probe on key_gen_turn_1_kout6
  // Probe on key_gen_turn_1_kout7
  // Probe on key_gen_turn_1_kout8
  // Probe on key_gen_turn_1_kout9
  // Probe on key_gen_turn_1_kout10
  // Probe on key_gen_turn_1_kout11
  // Probe on key_gen_turn_1_kout12
  // Probe on key_gen_turn_1_kout13
  // Probe on key_gen_turn_1_kout14
  // Probe on key_gen_turn_1_kout15
endmodule
